# Fritzing sketch schematic1 (saved by Fritzing 0.9.3b)
breadboards: 1

parts:
  Raspberry_Pi_1 = Raspberry Pi 3 [part_number=RPI-3-V1.2]
  LED3 = LED - 5mm [color="Red (633nm)" package="5 mm [THT]"]
  R3 = Resistor [tolerance=±5% resistance=220 package=THT]

nets:
  N1: Raspberry_Pi_1.GND, R3.Pin_1
  N2: Raspberry_Pi_1.GPIO24, LED3.anode
  N3: LED3.cathode, R3.Pin_0
